# Fritzing sketch ilifevirtualwall (saved by Fritzing 0.9.3b)

parts:
  Digispark1 = Digispark
  D1 = LTE-302 [package=lte-302]
  R1 = Resistor [tolerance=±5% resistance=100 package=THT]
  BAT1 = BC9VPC [package=bc9vpc]

nets:
  N1: Digispark1.GND, D1.A, BAT1.V-
  N2: Digispark1.VIN, BAT1.V+
  N3: D1.C, R1.Pin_1

custom parts:
  Digispark: The Digispark is an Attiny85 based microcontroller development board similar to the Arduino line, only cheaper, smaller, and a bit less powerful. With a whole host of shields to extend its functionality and the ability to use the familiar Arduino IDE the Digispark is a great way to jump into electronics, or perfect for when an Arduino is too big or too much.

// code stored in the sketch: ilifevirtualwall.ino
/*
 * Virtual Wall for iLife v7s
 * For ATtiny85 with Micronucleus bootloader
 * Plug a 940nm IRLed in pin1
 * Version 0.1 by @godlikebob
 * 
 * Notes: 
 *  - Import IRremote Library by shirriff
 *  - STL for 3d print available at Thingiverse.
 *  
 */
#include <IRremote.h>
#define DELAY 700

IRsend irsend;

void setup(){
}

void loop() {
  unsigned int rawData[17] = {9200,4600, 600,550, 600,1700, 600,550, 600,550, 600,1650, 600,550, 600,550, 600};
  irsend.sendRaw(rawData, 17, 38); 
  delay(DELAY);
}
